# Fritzing sketch protoboard (saved by Fritzing 0.9.2b)
breadboards: 1

parts:
  T1 = LM35 Temperature Sensor [package="TO92 [THT]"]
  T2 = LM35 Temperature Sensor [package="TO92 [THT]"]
  Parte1 = Intel Galileo
  PIR1 = PIR sensor

nets:
  5V: T1.+Vs, T2.+Vs, Parte1.5V, PIR1.VDD
  N1: T1.Vout, Parte1.A0
  GND: T1.GND, T2.GND, Parte1.GND, PIR1.GND
  N2: T2.Vout, Parte1.A2
  N3: Parte1.D2, PIR1.SIG
